# Fritzing sketch breadboard (saved by Fritzing 0.9.3b)
circuit board: 8.46667cm x 5.64444cm
breadboards: 1

parts:
  Part1 = Arduino Nano (Rev3.0)
  MCP42010 = IC, DIP package, 14 pins [chip_label=MCP42010]
  MCP42011 = IC, DIP package, 14 pins [chip_label=MCP42010]
  LED1 = smd LED [color="Red (633nm)" package="1206 [SMD]"]
  R1 = Resistor [tolerance=±5% resistance=220 package="0402 [SMD]"]
  C1 = Ceramic Capacitor [capacitance=100nF package="100 mil [THT, multilayer]"]
  C2 = Ceramic Capacitor [capacitance=100nF package="100 mil [THT, multilayer]"]
  LED2 = smd LED [color="Red (633nm)" package="1206 [SMD]"]
  LED3 = smd LED [color="Red (633nm)" package="1206 [SMD]"]
  LED4 = smd LED [color="Red (633nm)" package="1206 [SMD]"]
  R2 = Resistor [tolerance=±5% resistance=220 package="0402 [SMD]"]
  R3 = Resistor [tolerance=±5% resistance=220 package="0402 [SMD]"]
  R4 = Resistor [tolerance=±5% resistance=220 package="0402 [SMD]"]

nets:
  N1: Part1.GND, MCP42010.pin4, MCP42011.pin4, LED1.anode, C1.1, C2.1, LED2.anode, LED3.anode, LED4.anode
  N2: Part1.D2, R3.Pin_0
  N3: Part1.D3, R1.Pin_0
  N4: Part1.D4, R2.Pin_0
  N5: Part1.D6, LED1.cathode, R1.Pin_1, R4.Pin_0
  N6: Part1.D7, MCP42010.pin1
  N7: Part1.D8, MCP42011.pin1
  N8: Part1.D11/MOSI, MCP42010.pin3, MCP42011.pin3
  N9: Part1.5V, MCP42010.pin14, MCP42011.pin14, C1.0, C2.0
  N10: Part1.D13/SCK, MCP42010.pin2, MCP42011.pin2
  N11: LED2.cathode, R2.Pin_1
  N12: LED3.cathode, R3.Pin_1
  N13: LED4.cathode, R4.Pin_1
